# Fritzing sketch Sketch (saved by Fritzing 0.9.3b)
breadboards: 1

parts:
  Mod1 = ESP32 - CAM
  Driver1 = 28BYJ-48 Driver Module [part_number=ULN2003 package=THT]
  SM1 = 28BYJ-48 Stepper Motor [part_number=28BYJ-48]
  Power_plug1 = Power plug
  U3 = GAS_SENSOR [package=mq-3]

nets:
  N1: Mod1.IO12, Driver1.IN1
  N2: Mod1.IO13, Driver1.IN2
  N3: Mod1.IO15, Driver1.IN3
  N4: Mod1.IO14, Driver1.IN4
  N5: Mod1.IO2, U3.H2
  GND: Mod1.GND, Driver1.GND, Power_plug1.GND, U3.A1
  N6: Driver1.Vmotor, Power_plug1.VCC, U3.B1
  N7: Driver1.blue-pin, SM1.blue-pin
  N8: Driver1.pink-pin, SM1.pink-pin
  N9: Driver1.yellow-pin, SM1.yellow-pin
  N10: Driver1.orange-pin, SM1.orange-pin
  N11: Driver1.red-pin, SM1.red-pin

custom parts:
  ESP32 - CAM: The ESP32-CAM has a very competitive small-size camera module that can operate independently as a minimum system with a footprint of only 27*40.5*4.5mm and a deep sleep current of up to 6mA.
  28BYJ-48 Driver Module: ULN2003 Driver Module for the 28BYJ-48 Unipolar Stepper Motor LED A - Blue wire - Bottom coil left LED B - Pink wire - Top coil left LED C - Yellow wire - Bottom coil right LED D - Orange wire - Top coil right Common rail - red Connector pins: blue - pink - yellow - orange - red Control pins - IN1 to IN4 Power pins - GND & Vmotor (5-12V) On/Off jumper (if removed, power to motor is cut).
  28BYJ-48 Stepper Motor: Unipolar Stepper Motor 28BYJ-48 Top coil - pink & orange Bottom coil - blue & yellow Common rail - red Connector pins: blue - pink - yellow - orange - red
